// Logisim project Vending Machine.circ as structural Verilog: 1 circuit, main circuit main
module main (
  input  Clock,
  input  Dime,
  input  Nickel,
  output Q1,
  output Out,
  output Q0
);

  wire and_1_out, and_2_out, and_3_out, and_4_out, and_5_out, and_6_out, D0_qn, D1_qn, not_1_out, or_1_out,
       or_2_out;

  not not_1 (not_1_out, Nickel);
  and and_1 (and_1_out, D1_qn, Dime);
  and and_2 (and_2_out, D1_qn, Q0, Nickel);
  and and_3 (and_3_out, D0_qn, Q1);
  and and_4 (and_4_out, D0_qn, Nickel);
  and and_5 (and_5_out, D1_qn, Q0, not_1_out);
  and and_6 (and_6_out, Q1, D0_qn, Dime);
  or or_1 (or_1_out, and_1_out, and_2_out, and_3_out);
  or or_2 (or_2_out, and_4_out, and_5_out, and_6_out);
  D_Flip_Flop D1 (.clk(Clock), .D(or_1_out), .Q(Q1), .Qn(D1_qn));  // open: preset, en, reset
  and and_7 (Out, Q1, Q0);
  D_Flip_Flop D0 (.clk(Clock), .D(or_2_out), .Q(Q0), .Qn(D0_qn));  // open: preset, en, reset
endmodule
